# Fritzing sketch practice2-breadboard (saved by Fritzing 0.9.2b)
breadboards: 1

parts:
  パーツ1 = Arduino Uno (Rev3)
  LED1 = LED - 5mm [color="Red (633nm)" package="5 mm [THT]"]
  R1 = Resistor [tolerance=±5% resistance=470 package=THT]
  S1 = Pushbutton [package="[THT]"]
  R2 = Resistor [tolerance=±5% resistance=10k package=THT]

nets (from the breadboard view):
  N1: パーツ1.D13/SCK, LED1.cathode
  N2: パーツ1.GND, S1.Pin_3, S1.Pin_4
  N3: パーツ1.D7, S1.Pin_1, S1.Pin_2, R2.Pin_0
  N4: パーツ1.5V, R1.Pin_0, R2.Pin_1
  N5: LED1.anode, R1.Pin_1
