# Fritzing sketch practice4-breadboard (saved by Fritzing 0.9.2b)
breadboards: 1

parts:
  R1 = Resistor [tolerance=±5% resistance=330 package=THT]
  R3 = PHOTOCELL [package=photocell-kit]
  R2 = Resistor [tolerance=±5% resistance=10k package=THT]
  LED1 = LED - 5mm [color="Red (633nm)" package="5 mm [THT]"]
  パーツ1 = Arduino Uno (Rev3)

nets:
  N1: R1.Pin_0, R2.Pin_1, パーツ1.GND
  N2: R1.Pin_1, LED1.cathode
  N3: R3.P$1, パーツ1.5V
  N4: R3.P$2, R2.Pin_0, パーツ1.A0
  N5: LED1.anode, パーツ1.D11_PWM/MOSI
