# Fritzing sketch practice4-breadboard_volume (saved by Fritzing 0.9.3b)
breadboards: 1

parts:
  R1 = Resistor [tolerance=±5% resistance=330 package=THT]
  LED1 = LED - 5mm [color="Red (633nm)" package="5 mm [THT]"]
  パーツ1 = Arduino Uno (Rev3)
  R4 = Trimmer Potentiometer [maximum_resistance=10kΩ package=THT]

nets:
  N1: R1.Pin_0, パーツ1.GND, R4.leg2
  N2: R1.Pin_1, LED1.cathode
  N3: LED1.anode, パーツ1.D11_PWM/MOSI
  N4: パーツ1.A0, R4.wiper
  N5: パーツ1.5V, R4.leg1
