# Fritzing sketch practice7 (saved by Fritzing 0.9.3b)
breadboards: 1

parts:
  U1 = TA7291P [package=HSIP10-P-2.54(THT)]
  パーツ1 = Arduino Uno (Rev3) - ICSP
  R1 = Resistor [tolerance=±5% resistance=4.7k package=THT]
  M1 = DC Motor
  VCC1 = Battery

nets:
  GND: U1.GND, パーツ1.GND, VCC1.-
  N1: U1.OUT1, M1.pin_1
  N2: U1.Vref, R1.Pin_0
  N3: U1.IN1, パーツ1.D11_PWM/MOSI
  N4: U1.IN2, パーツ1.D10_PWM/SS
  N5: U1.Vcc, U1.Vs, R1.Pin_1, VCC1.+
  N6: U1.OUT2, M1.pin_2

custom parts:
  TA7291P: The IC are Full-Bridge Driver. 4 modes available (CW / CCW / STOP / BRAKE) and PWM control. Output current:1.0 A (AVE.) 2.0 A (PEAK)
